// Digital circuit DigitalAlarm.dig as structural Verilog
module DigitalAlarm (
  input  CLK,
  input  INC,
  input  SET,
  input  CLR,
  output [6:0] SEC_SEG_1,
  output [6:0] SEC_SEG_2,
  output [6:0] MIN_SEG_1,
  output [6:0] MIN_SEG_2,
  output [6:0] HR_SEG_1,
  output [6:0] HR_SEG_2
);

  wire and_1_out, and_2_out, or_1_out;
  wire [4:0] clockdev_1_hour;
  wire [5:0] clockdev_1_min, clockdev_1_sec;

  and and_1 (and_1_out, CLK, ~SET);  // And
  and and_2 (and_2_out, SET, INC);
  or or_1 (or_1_out, and_1_out, and_2_out);
  ClockDev clockdev_1 (
    .EN(1'b1), .CLR(CLR), .CLK(or_1_out), .SEC(clockdev_1_sec), .MIN(clockdev_1_min), .HOUR(clockdev_1_hour));
  _2DisplayDriver _2displaydriver_1 (.DATA_IN(clockdev_1_sec), .SEG_1(SEC_SEG_1), .SEG_2(SEC_SEG_2));
  _2DisplayDriver _2displaydriver_2 (.DATA_IN(clockdev_1_min), .SEG_1(MIN_SEG_1), .SEG_2(MIN_SEG_2));
  _2DisplayDriver _2displaydriver_3 (.DATA_IN({1'b0, clockdev_1_hour}), .SEG_1(HR_SEG_1), .SEG_2(HR_SEG_2));

  // Notes on the sheet:
  //   CLK: Hz: 2
endmodule
